# Fritzing sketch First Board (saved by Fritzing 0.9.4)
breadboards: 1

parts:
  Part1 = Arduino Uno (Rev3) - ICSP
  LED1 = LED - 5mm [color="Red (633nm)" package="5 mm [THT]"]

nets:
  N1: Part1.D3_PWM, LED1.anode
  N2: Part1.GND, LED1.cathode
