# Fritzing sketch board (saved by Fritzing 0.9.4)
breadboards: 1

parts:
  Part1 = Arduino Uno (Rev3) - ICSP
  LED1 = smd LED [color="Red (633nm)" package="1206 [SMD]"]

nets:
  N1: Part1.D2, LED1.anode
  N2: Part1.GND, LED1.cathode
